# Fritzing sketch AlzFinderMoboV0.1 (saved by Fritzing 0.9.2b)
circuit board: 8.0204cm x 5.45133cm
breadboards: 1

parts:
  JP1 = FTDI_BASIC [package=ftdi_basic]
  JP2 = FTDI_BASIC [package=ftdi_basic]
  JP3 = FTDI_BASIC [package=ftdi_basic]  # not connected
  JP4 = FTDI_BASIC [package=ftdi_basic]  # not connected
  J2 = female pin header, 2 pins [form="♀ (female)"]
  JP = female pin header, 2 pins [form="♀ (female)"]
  JP5 = FTDI_BASIC [package=ftdi_basic]
  JP6 = FTDI_BASIC [package=ftdi_basic]  # not connected
  Q1 = TRANSISTOR_PNP [package=to-92]
  R2 = Resistor [tolerance=±5% resistance=220 package=THT]
  R1 = Resistor [tolerance=±5% resistance=220 package=THT]
  Teensy_3_1 = Teensy 3.1

nets:
  N1: JP1.1, Teensy_3_1.D0
  N2: JP2.5, Teensy_3_1.D6
  N3: JP2.6, Teensy_3_1.D1
  4.1V: J2.pin1, JP.pin2, Q1.E, R2.Pin_1
  GND: J2.pin2, JP5.6, Teensy_3_1.GND
  N4: JP.pin1, Teensy_3_1.Vin
  N5: JP5.1, Q1.C
  N6: JP5.2, Teensy_3_1.D9
  N7: JP5.3, Teensy_3_1.D10
  N8: Q1.B, R2.Pin_0, R1.Pin_1
  N9: R1.Pin_0, Teensy_3_1.D8

notes:
  Alzheimer's Finder MOBO, 0.1
  AlzFinder ver 0.1
